# Fritzing sketch Circuit_Diagram (saved by Fritzing 0.9.3b)
breadboards: 1

parts:
  Raspberry_Pi_1 = Raspberry Pi 3 [part_number=RPI-3-V1.2]
  M2_Left_Motor = Basic Servo
  VCC1 = 4 x AAA Battery Mount
  M1_Right_Motor = Basic Servo

nets:
  N1: Raspberry_Pi_1.GIPO6, M2_Left_Motor.pulse
  N2: Raspberry_Pi_1.GIPO19, M1_Right_Motor.pulse
  GND: Raspberry_Pi_1.GND, M2_Left_Motor.gnd, VCC1.-, M1_Right_Motor.gnd
  VCC: M2_Left_Motor.vcc, VCC1.+, M1_Right_Motor.vcc

notes:
  [OpEdRo] : https://github.com/stteff/An-Open-Educational-RPi-Robot
  GND  OUT  VCC
  VCC OUT GND
  Left Photoelectric Sensor
  Right Photoelectric Sensor
