# Fritzing sketch OpEdRo Circuit Diagram_1 (saved by Fritzing 0.9.3b)
breadboards: 2

parts:
  M2_Left_Motor = Basic Servo
  VCC1 = 4 x AAA Battery Mount
  M1_Right_Motor = Basic Servo
  Ultrasonic_(hc-sr04) = hc-sr04
  Thermometer = DS18B20 1-Wire Temperature Sensor [part_number=DS18B20]
  R1 = Resistor [tolerance=±5% resistance=4.7k package=THT]
  R4 = Resistor [tolerance=±5% resistance=1k package=THT]
  R3 = Resistor [tolerance=±5% resistance=1k package=THT]
  R2 = Resistor [tolerance=±5% resistance=1k package=THT]
  Raspberry_Pi_1 = Raspberry Pi 3 [part_number=RPI-3-V1.2]

nets:
  GND: M2_Left_Motor.gnd, VCC1.-, M1_Right_Motor.gnd, Thermometer.GND, R4.Pin_0, Raspberry_Pi_1.GND
  VCC: M2_Left_Motor.vcc, VCC1.+, M1_Right_Motor.vcc
  N1: M2_Left_Motor.pulse, Raspberry_Pi_1.GIPO6
  N2: M1_Right_Motor.pulse, Raspberry_Pi_1.GIPO19
  N3: Ultrasonic_(hc-sr04).Trig, Raspberry_Pi_1.5V
  N4: Ultrasonic_(hc-sr04).Echo, Raspberry_Pi_1.GIPO17
  N5: Ultrasonic_(hc-sr04).GND, R3.Pin_0
  N6: Thermometer.DQ, R1.Pin_1, Raspberry_Pi_1.GIPO4
  VDD: Thermometer.VDD, R1.Pin_0, Raspberry_Pi_1.3v3
  N7: R4.Pin_1, R2.Pin_1
  N8: R3.Pin_1, R2.Pin_0, Raspberry_Pi_1.GIPO18

notes:
  [OpEdRo] : https://github.com/stteff/An-Open-Educational-RPi-Robot
  GND  OUT  VCC
  VCC OUT GND
  Left Photoelectric Sensor
  Right Photoelectric Sensor
